# Fritzing sketch Fritzing HC05 Seperate Diagram (saved by Fritzing 0.9.3b)
breadboards: 1

parts:
  Part2 = Arduino Mega 2560 (Rev3)  # not connected
  Part3 = Bluetooth HC-05 Macho  # not connected
  R1 = Resistor [tolerance=±5% resistance=220 package=THT]
  R2 = Resistor [tolerance=±5% resistance=220 package=THT]

nets:
  N1: R1.Pin_1, R2.Pin_0

notes:
  Water Flow Rate Sensor
